// Logisim project DataPath.circ as structural Verilog
module Register_File_32x32_bits (
  input  [31:0] in_1,
  input  [4:0] DA,
  input  [31:0] DI,
  input  R_W,
  input  [4:0] SA,
  input  [4:0] SB,
  input  Clk,
  input  Reset,
  input  [31:0] Lo,
  input  [31:0] Hi,
  input  LH_RW,
  output [31:0] Data_A,
  output [31:0] Data_B,
  output [31:0] Lo_2,
  output [31:0] Hi_2
);

  wire L1, L2, L3, L4, L5, L6, L7, L8, L9, L10, L11, L12, L13, L14, L15, L16, L17, L18, L19, L20, L21, L22,
       L23, L24, L25, L26, L27, L28, L29, L30, L31;
  wire [31:0] R1, R2, R3, R4, R5, R6, R7, R8, R9, R10, R11, R12, R13, R14, R15, R16, R17, R18, R19, R20, R21,
       R22, R23, R24, R25, R26, R27, R28, R29, R30, R31;

  Decoder #(.select(5)) decoder_1 (
    .out1(L1), .out2(L2), .out3(L3), .out4(L4), .out5(L5), .out6(L6), .out7(L7), .out8(L8), .out9(L9),
    .out10(L10), .out11(L11), .out12(L12), .out13(L13), .out14(L14), .out15(L15), .out16(L16), .out17(L17),
    .out18(L18), .out19(L19), .out20(L20), .out21(L21), .out22(L22), .out23(L23), .out24(L24), .out25(L25),
    .out26(L26), .out27(L27), .out28(L28), .out29(L29), .out30(L30), .out31(L31), .sel(DA), .en(R_W));  // open: out0
  Register_32_bits register_32_bits_1 (.Data_In(Lo), .Load(LH_RW), .Clock(Clk), .Reset(Reset), .Current_Value(Lo_2));
  Register_32_bits register_32_bits_2 (.Data_In(Hi), .Load(LH_RW), .Clock(Clk), .Reset(Reset), .Current_Value(Hi_2));
  Register_32_bits register_32_bits_3 (.Data_In(DI), .Load(L1), .Clock(Clk), .Reset(Reset), .Current_Value(R1));
  Register_32_bits register_32_bits_4 (.Data_In(DI), .Load(L2), .Clock(Clk), .Reset(Reset), .Current_Value(R2));
  Register_32_bits register_32_bits_5 (.Data_In(DI), .Load(L3), .Clock(Clk), .Reset(Reset), .Current_Value(R3));
  Register_32_bits register_32_bits_6 (.Data_In(DI), .Load(L4), .Clock(Clk), .Reset(Reset), .Current_Value(R4));
  Register_32_bits register_32_bits_7 (.Data_In(DI), .Load(L5), .Clock(Clk), .Reset(Reset), .Current_Value(R5));
  Register_32_bits register_32_bits_8 (.Data_In(DI), .Load(L6), .Clock(Clk), .Reset(Reset), .Current_Value(R6));
  Register_32_bits register_32_bits_9 (.Data_In(DI), .Load(L7), .Clock(Clk), .Reset(Reset), .Current_Value(R7));
  Register_32_bits register_32_bits_10 (.Data_In(DI), .Load(L8), .Clock(Clk), .Reset(Reset), .Current_Value(R8));
  Register_32_bits register_32_bits_11 (.Data_In(DI), .Load(L9), .Clock(Clk), .Reset(Reset), .Current_Value(R9));
  Register_32_bits register_32_bits_12 (.Data_In(DI), .Load(L10), .Clock(Clk), .Reset(Reset), .Current_Value(R10));
  Register_32_bits register_32_bits_13 (.Data_In(DI), .Load(L11), .Clock(Clk), .Reset(Reset), .Current_Value(R11));
  Register_32_bits register_32_bits_14 (.Data_In(DI), .Load(L12), .Clock(Clk), .Reset(Reset), .Current_Value(R12));
  Register_32_bits register_32_bits_15 (.Data_In(DI), .Load(L13), .Clock(Clk), .Reset(Reset), .Current_Value(R13));
  Register_32_bits register_32_bits_16 (.Data_In(DI), .Load(L14), .Clock(Clk), .Reset(Reset), .Current_Value(R14));
  Register_32_bits register_32_bits_17 (.Data_In(DI), .Load(L15), .Clock(Clk), .Reset(Reset), .Current_Value(R15));
  Register_32_bits register_32_bits_18 (.Data_In(DI), .Load(L16), .Clock(Clk), .Reset(Reset), .Current_Value(R16));
  Register_32_bits register_32_bits_19 (.Data_In(DI), .Load(L17), .Clock(Clk), .Reset(Reset), .Current_Value(R17));
  Register_32_bits register_32_bits_20 (.Data_In(DI), .Load(L18), .Clock(Clk), .Reset(Reset), .Current_Value(R18));
  Register_32_bits register_32_bits_21 (.Data_In(DI), .Load(L19), .Clock(Clk), .Reset(Reset), .Current_Value(R19));
  Register_32_bits register_32_bits_22 (.Data_In(DI), .Load(L20), .Clock(Clk), .Reset(Reset), .Current_Value(R20));
  Register_32_bits register_32_bits_23 (.Data_In(DI), .Load(L21), .Clock(Clk), .Reset(Reset), .Current_Value(R21));
  Register_32_bits register_32_bits_24 (.Data_In(DI), .Load(L22), .Clock(Clk), .Reset(Reset), .Current_Value(R22));
  Register_32_bits register_32_bits_25 (.Data_In(DI), .Load(L23), .Clock(Clk), .Reset(Reset), .Current_Value(R23));
  // Register_32_bits register_32_bits_26: pin names not known; wires that end beside it: DI, L24, Clk, Reset, R24
  // Register_32_bits register_32_bits_27: pin names not known; wires that end beside it: DI, L25, Clk, Reset, R25
  // Register_32_bits register_32_bits_28: pin names not known; wires that end beside it: DI, L26, Clk, Reset, R26
  // Register_32_bits register_32_bits_29: pin names not known; wires that end beside it: DI, L27, Clk, Reset, R27
  // Register_32_bits register_32_bits_30: pin names not known; wires that end beside it: DI, L28, Clk, Reset, R28
  // Register_32_bits register_32_bits_31: pin names not known; wires that end beside it: DI, L29, Clk, Reset, R29
  // Register_32_bits register_32_bits_32: pin names not known; wires that end beside it: DI, L30, Clk, Reset, R30
  // Register_32_bits register_32_bits_33: pin names not known; wires that end beside it: DI, L31, Clk, Reset, R31
  Multiplexer #(.select(5), .width(32), .enable("false")) multiplexer_1 (
    .in0(in_1), .in1(R1), .in2(R2), .in3(R3), .in4(R4), .in5(R5), .in6(R6), .in7(R7), .in8(R8), .in9(R9),
    .in10(R10), .in11(R11), .in12(R12), .in13(R13), .in14(R14), .in15(R15), .in16(R16), .in17(R17),
    .in18(R18), .in19(R19), .in20(R20), .in21(R21), .in22(R22), .in23(R23), .in24(R24), .in25(R25),
    .in26(R26), .in27(R27), .in28(R28), .in29(R29), .in30(R30), .in31(R31), .out(Data_A), .sel(SA));
  Multiplexer #(.select(5), .width(32), .enable("false")) multiplexer_2 (
    .in0(in_1), .in1(R1), .in2(R2), .in3(R3), .in4(R4), .in5(R5), .in6(R6), .in7(R7), .in8(R8), .in9(R9),
    .in10(R10), .in11(R11), .in12(R12), .in13(R13), .in14(R14), .in15(R15), .in16(R16), .in17(R17),
    .in18(R18), .in19(R19), .in20(R20), .in21(R21), .in22(R22), .in23(R23), .in24(R24), .in25(R25),
    .in26(R26), .in27(R27), .in28(R28), .in29(R29), .in30(R30), .in31(R31), .out(Data_B), .sel(SB));

  // Other names for the same wires on the sheet: Hi_t[31:0] = Hi_2; Lo_t[31:0] = Lo_2; LoHiRW = LH_RW;
  //   R0[31:0] = in_1; Rst = Reset

  // Notes on the sheet:
  //   Inputs
  //   Data Address
  //   Data In
  //   Read/Write
  //   Selector A
  //   Selector B
  //   Lo HIi R/W
  //   Lo
  //   Hi
  //   Outputs
endmodule

module Register_32_bits (
  input  [31:0] Data_In,
  input  Load,
  input  Clock,
  input  Reset,
  output [31:0] Current_Value
);

  Register #(.width(32)) register_1 (.D(Data_In), .en(Load), .Q(Current_Value), .clk(Clock), .clr(Reset));

  // Notes on the sheet:
  //   Register 32 bits
endmodule

module Test_Register_File (
  input  [4:0] in_1,
  input  [4:0] in_2,
  input  [31:0] in_3,
  input  [4:0] in_4,
  input  in_5,
  input  in_6,
  output [31:0] out_7,
  output [31:0] out_8
);

  wire register_file_32x32_bits_1_p6;

  // Probe on in_3
  // Register_File_32x32_bits register_file_32x32_bits_1: pin names not known; wires that end beside it: in_1, in_2, in_3, in_4, in_5, register_file_32x32_bits_1_p6
  Clock clock_1 (.out(register_file_32x32_bits_1_p6));
  // Probe on out_7
  // Probe on out_8
endmodule

module ALU_2 (
  input  [31:0] A,
  input  [31:0] B,
  input  [3:0] S,
  output [31:0] R,
  output Zero,
  output Negative,
  output [31:0] Lo,
  output [31:0] Hi
);

  wire comparator_1_lt, comparator_2_lt;
  wire [31:0] And, Diff, HiDiv, HiDivu, HiMult, HiMulu, LoDiv, LoDivu, LoMult, LoMulu, Nor, Or, slt, sltu,
       Sum, Xor;

  Adder #(.width(32)) adder_1 (.a(A), .b(B), .out(Sum));  // open: cin, cout
  Subtractor #(.width(32)) subtractor_1 (.a(A), .b(B), .out(Diff));  // open: bin, bout
  assign And = A & B;  // AND_Gate and_1, 32 bits wide
  assign Or = A | B;  // OR_Gate or_1, 32 bits wide
  assign Nor = ~Or;  // NOT_Gate not_1, 32 bits wide
  assign Xor = A ^ B;  // XOR_Gate xor_1, 32 bits wide
  Multiplier #(.width(32)) multiplier_1 (.a(A), .b(B), .out(LoMulu), .cout(HiMulu));  // open: cin
  Signed_MUltiplier signed_multiplier_1 (.A(A), .B(B), .Low(LoMult), .High(HiMult));
  Comparator #(.width(32)) comparator_1 (.a(A), .b(B), .lt(comparator_1_lt));  // open: gt, eq
  assign slt = {{31{1'b0}}, comparator_1_lt};  // Bit_Extender bit_extender_1
  Comparator #(.width(32), .mode("unsigned")) comparator_2 (.a(A), .b(B), .lt(comparator_2_lt));  // open: gt, eq
  assign sltu = {{31{1'b0}}, comparator_2_lt};  // Bit_Extender bit_extender_2
  Divider #(.width(32)) divider_1 (.a(A), .b(B), .out(LoDivu), .rem(HiDivu));  // open: upper
  Signed_Div signed_div_1 (.A(A), .B(B), .Low(LoDiv), .High(HiDiv));
  Multiplexer #(.select(4), .width(32), .enable("false")) multiplexer_1 (.out(R));  // open: in0, in1, in2, in3, in4, in5, in6, in7, in8, in9, in10, in11, in12, in13, in14, in15, sel
  Multiplexer #(.select(2), .width(32), .enable("false")) multiplexer_2 (
    .out(Lo), .sel(S[3:2]));  // open: in0, in1, in2, in3
  Multiplexer #(.select(2), .width(32), .enable("false")) multiplexer_3 (
    .out(Hi), .sel(S[3:2]));  // open: in0, in1, in2, in3
  Comparator #(.width(32)) comparator_3 (.a(R), .b({32{1'b0}}), .eq(Zero), .lt(Negative));  // open: gt

  // Other names for the same wires on the sheet: LoHi_S[1:0] = S[3:2]

  // Notes on the sheet:
  //   ALU
  //   Arithmetic Ops
  //   Logic Ops
  //   Unisgned
endmodule

module Test_ALU (
  input  [31:0] in_1,
  input  [3:0] in_2,
  input  [31:0] in_3,
  output out_4,
  output out_5,
  output [31:0] out_6
);

  // Probe on in_1
  // Probe on in_3
  // Probe on out_6
  // ALU_2 alu_1: pin names not known; wires that end beside it: in_1, in_3, in_2, out_4, out_5, out_6
endmodule

module Signed_MUltiplier (
  input  [31:0] A,
  input  [31:0] B,
  output [31:0] Low,
  output [31:0] High
);

  wire adder_2_cout, Sign_A, Sign_B, Sign_R;
  wire [31:0] abs_1_out, abs_2_out, minus_High, minus_Low, not_1_out, not_2_out, plus_High, plus_Low;

  // Probe on A
  // Probe on B
  Adder #(.width(1)) adder_1 (.a(Sign_A), .b(Sign_B), .out(Sign_R));  // open: cin, cout
  ABS abs_1 (.In(A), .Out(abs_1_out), .Sign(Sign_A));
  ABS abs_2 (.In(B), .Out(abs_2_out), .Sign(Sign_B));
  Multiplier #(.width(32)) multiplier_1 (.a(abs_1_out), .b(abs_2_out), .out(plus_Low), .cout(plus_High));  // open: cin
  assign not_1_out = ~plus_Low;  // NOT_Gate not_1, 32 bits wide
  Adder #(.width(32)) adder_2 (.a(not_1_out), .b(32'h1), .out(minus_Low), .cout(adder_2_cout));  // open: cin
  assign not_2_out = ~plus_High;  // NOT_Gate not_2, 32 bits wide
  Adder #(.width(32)) adder_3 (.a(not_2_out), .b({32{1'b0}}), .out(minus_High), .cin(adder_2_cout));  // open: cout
  // Probe on Low
  Multiplexer #(.width(32), .enable("false")) multiplexer_1 (.in0(plus_Low), .in1(minus_Low), .out(Low), .sel(Sign_R));
  Multiplexer #(.width(32), .enable("false")) multiplexer_2 (
    .in0(plus_High), .in1(minus_High), .out(High), .sel(Sign_R));
  // Probe on High

  // Notes on the sheet:
  //   Final Sign
  //   Signed Multiplier
  //   Negator
  //   1) Multiply the operand's absolute value
  //   2) Invert the result if neccesary according to the signs of the operands
  //   Outputs
endmodule

module Signed_Div (
  input  [31:0] A,
  input  [31:0] B,
  output [31:0] Low,
  output [31:0] High
);

  wire Sign_A, Sign_B, Sign_Quo;
  wire [31:0] abs_1_out, abs_2_out, minus_Quo, minus_Rem, plus_Quo, plus_Rem;

  // Probe on A
  // Probe on B
  ABS abs_1 (.In(A), .Out(abs_1_out), .Sign(Sign_A));
  ABS abs_2 (.In(B), .Out(abs_2_out), .Sign(Sign_B));
  xor xor_1 (Sign_Quo, Sign_A, Sign_B);
  Divider #(.width(32)) divider_1 (.a(abs_1_out), .b(abs_2_out), .out(plus_Quo), .rem(plus_Rem));  // open: upper
  Negator #(.width(32)) negator_1 (.in(plus_Quo), .out(minus_Quo));
  Negator #(.width(32)) negator_2 (.in(plus_Rem), .out(minus_Rem));
  // Probe on Low
  Multiplexer #(.width(32), .enable("false")) multiplexer_1 (
    .in0(plus_Quo), .in1(minus_Quo), .out(Low), .sel(Sign_Quo));
  Multiplexer #(.width(32), .enable("false")) multiplexer_2 (.in0(plus_Rem), .in1(minus_Rem), .out(High), .sel(Sign_A));
  // Probe on High

  // Notes on the sheet:
  //   Signed Divider
  //   Quotient Sign
  //   Negator
  //   1) Divide the operand's absolute value
  //   2) Negate the quotient if the signs of the operands are opposite
  //   3) Make the sign of the remainder match the dividend
  //   Outputs
endmodule

module ABS (
  input  [31:0] In,
  output [31:0] Out,
  output Sign
);

  wire [31:0] negator_1_out;

  Negator #(.width(32)) negator_1 (.in(In), .out(negator_1_out));
  BitSelector #(.width(32)) bitselector_1 (.in(In), .out(Sign), .sel({5{1'b1}}));
  Multiplexer #(.width(32), .enable("false")) multiplexer_1 (.in0(In), .in1(negator_1_out), .out(Out), .sel(Sign));
endmodule

module Branch_Control_2 (
  input  [31:0] PC_in,
  input  jump,
  input  flag,
  input  [15:0] offset,
  output [31:0] PC_out
);


  // Notes on the sheet:
  //   Direccion de la
  //   Instruccion Actual
  //   Instruccion de Salto
  //   Condicion de Salto
  //   Tamanno de Salto (k)
  //   Direccion de la
  //   Proxima Instruccion
endmodule

module Test_Branch_Control (
  input  [31:0] in_1,
  input  in_2,
  input  in_3,
  input  [15:0] in_4,
  output [31:0] out_5
);

  // Probe on in_1
  // Probe on in_4
  Branch_Control_2 branch_control_1 (.PC_in(in_1), .jump(in_2), .flag(in_3), .offset(in_4), .PC_out(out_5));
  // Probe on out_5
endmodule
