// Logisim project RAM Interface.circ as structural Verilog: 2 circuits, main circuit Endian Converter
module MemoryManager (
  input  [31:0] Addres_In,
  input  [31:0] Ram_out_0,
  input  [31:0] Ram_out_1,
  input  [31:0] Ram_out_2,
  input  [31:0] Ram_out_3,
  input  [3:0] Read_Time,
  input  Clk,
  input  Rst,
  input  [3:0] Write_Time,
  input  Start,
  input  R_W,
  output [31:0] From_RAM,
  output [3:0] Mask,
  output [15:0] ADDR,
  output [1:0] Bank,
  output RAMReady,
  output Chip_Select,
  output RAM_Write
);

  wire comparator_1_lt, Count, demultiplexer_1_out0, demultiplexer_1_out1, IsFetch, or_2_out, Wait_q;
  wire [3:0] counter_1_q, Time;
  wire [31:0] RAM_OUT_0_t, RAM_OUT_1_t, RAM_OUT_2_t, RAM_OUT_3_t;

  Multiplexer #(.width(4), .enable("false")) multiplexer_1 (.in0(Read_Time), .in1(Write_Time), .out(Time), .sel(R_W));
  Endian_Converter endian_converter_1 (.Input(Ram_out_0), .Output(RAM_OUT_0_t));
  Endian_Converter endian_converter_2 (.Input(Ram_out_1), .Output(RAM_OUT_1_t));
  Endian_Converter endian_converter_3 (.Input(Ram_out_2), .Output(RAM_OUT_2_t));
  Endian_Converter endian_converter_4 (.Input(Ram_out_3), .Output(RAM_OUT_3_t));
  D_Flip_Flop Wait (.clk(Clk), .D(demultiplexer_1_out0), .Q(Wait_q));  // open: Qn, preset, en, reset
  or or_1 (Count, Wait_q, Start);
  Counter #(.width(4), .max('hf)) counter_1 (
    .count(Count), .Q(counter_1_q), .clk(Clk), .clr(or_2_out));  // open: load, D, carry
  or or_2 (or_2_out, Rst, RAMReady);
  Demultiplexer #(.enable("false")) demultiplexer_1 (
    .out0(demultiplexer_1_out0), .out1(demultiplexer_1_out1), .in(Count), .sel(IsFetch));
  Comparator #(.width(4), .mode("unsigned")) comparator_1 (
    .a(counter_1_q), .b(Time), .lt(comparator_1_lt));  // open: gt, eq
  not not_1 (IsFetch, comparator_1_lt);
  D_Flip_Flop End (.clk(Clk), .D(demultiplexer_1_out1), .Q(RAMReady));  // open: Qn, preset, en, reset
  Decoder #(.select(2), .enable("false")) decoder_1 (
    .out0(Mask[0]), .out1(Mask[1]), .out2(Mask[2]), .out3(Mask[3]), .sel(Addres_In[1:0]));
  Multiplexer #(.select(2), .width(32), .enable("false")) multiplexer_2 (
    .in0(RAM_OUT_0_t), .in1(RAM_OUT_1_t), .in2(RAM_OUT_2_t), .in3(RAM_OUT_3_t), .out(From_RAM),
    .sel(Addres_In[1:0]));
  or or_3 (Chip_Select, RAMReady, Count);
  and and_1 (RAM_Write, R_W, Count);

  assign ADDR = Addres_In[17:2];
  assign Bank = Addres_In[1:0];

  // Other names for the same wires on the sheet: Block[15:0] = Addres_In[17:2]; Clear = RAMReady; CS1 = RAMReady;
  //   End = RAMReady; CS0 = Count; RAM_Wr = Count; RW = R_W

  // Notes on the sheet:
  //   ADDRESS
  //   DATA FROM RAM
  //   RAM TIMING
  //   CONTROL SIGNALS
  //   TIMER
  //   FLOW CONTROL
endmodule

module Endian_Converter (
  input  [31:0] Input,
  output [31:0] Output
);


  assign Output = {Input[7:0], Input[15:8], Input[23:16], Input[31:24]};
endmodule
