// Logisim project s-mips.circ as structural Verilog: 4 circuits, main circuit S-MIPS Board
module S_MIPS_Board (
  input  DESHABILITAR_DISPATCHER,
  output halt
);

  wire and_1_out, button_1_out, CLK, CS, d_ff_1_q, d_ff_1_qn, LCLR, LoadRAM, LoadRAMOn, LW, R_R_W, R_W,
       ram_dispatcher_1_finished, RCS, Reset_out, RST, TTY_EN, undriven, undriven_2;
  wire [2:0] KDB;
  wire [3:0] LMask, Mask, ram_1_out_14, ram_1_write_time, RMask;
  wire [6:0] KDB_DATA, TTY_DATA;
  wire [15:0] Addr, LAddr, RAddr;
  wire [31:0] I0, I1, I2, I3, LData, multiplexer_4_out, ram_1_data_out_0, ram_1_data_out_1, ram_1_data_out_2,
       ram_1_data_out_3, ram_dispatcher_1_data, RI1, RI2, RI3;

  TTY #(.rows(25), .cols(80)) tty_1 (.data(TTY_DATA), .clk(CLK), .we(TTY_EN), .clr(RST));
  not not_1 (LoadRAMOn, ram_dispatcher_1_finished);
  RAM_Dispatcher ram_dispatcher_1 (
    .WriteTime(ram_1_write_time), .Clock(CLK), .Data(ram_dispatcher_1_data), .Address(LAddr), .Mask(LMask),
    .Finished(ram_dispatcher_1_finished), .Write(LW), .CLR(LCLR));
  RAM ram_1 (
    .Address(RAddr), .Data_Out_0(ram_1_data_out_0), .Data_Out_1(ram_1_data_out_1),
    .Data_Out_2(ram_1_data_out_2), .Data_Out_3(ram_1_data_out_3), .Data_In_0(I1), .Data_In_1(RI1),
    .Data_In_2(RI2), .Data_In_3(RI3), .Mask(RMask), .nRead_Write(R_R_W), .Chip_Select(RCS),
    .out_14(ram_1_out_14), .Reset(button_1_out), .Write_Time(ram_1_write_time));
  Button button_1 (.out(button_1_out));
  D_Flip_Flop d_ff_1 (
    .clk(CLK), .D(1'b1), .Q(d_ff_1_q), .Qn(d_ff_1_qn), .preset(undriven), .en(undriven_2), .reset(Reset_out));
  D_Flip_Flop d_ff_2 (
    .clk(CLK), .D(1'b1), .Q(d_ff_1_q), .Qn(d_ff_1_qn), .preset(undriven), .en(undriven_2), .reset(Reset_out));
  Button Reset (.out(Reset_out));
  // S_MIPS s_mips_1: pin names not known; wires that end beside it: Addr, ram_1_data_out_0, ram_1_data_out_1, ram_1_data_out_2, ram_1_data_out_3, I0, CS, I2, I3, Mask, ram_1_out_14, RST, ram_1_write_time, CLK, CS, CS, halt, TTY_EN, TTY_DATA, KDB[0], KDB[1], KDB[2], KDB_DATA
  D_Flip_Flop d_ff_3 (.clk(CLK), .D(d_ff_1_q), .Qn(LCLR), .reset(Reset_out));  // open: Q, preset, en
  or or_1 (RST, LCLR, LoadRAM);
  Clock clock_1 (.out(CLK));
  Multiplexer #(.width(32), .enable("false")) multiplexer_1 (.in0(I0), .in1(LData), .out(I1), .sel(LoadRAM));
  Multiplexer #(.width(32), .enable("false")) multiplexer_2 (.in0(I1), .in1(LData), .out(RI1), .sel(LoadRAM));
  Multiplexer #(.width(32), .enable("false")) multiplexer_3 (.in0(I2), .in1(LData), .out(RI2), .sel(LoadRAM));
  Multiplexer #(.width(32), .enable("false")) multiplexer_4 (
    .in0(I3), .in1(LData), .out(multiplexer_4_out), .sel(LoadRAM));
  and and_1 (and_1_out, ~DESHABILITAR_DISPATCHER, LoadRAMOn);  // AND_Gate
  Multiplexer #(.width(16), .enable("false")) multiplexer_5 (.in0(Addr), .in1(I3[15:0]), .out(RAddr), .sel(LoadRAM));
  Multiplexer #(.width(4), .enable("false")) multiplexer_6 (.in0(RMask), .in1(LMask), .out(RMask), .sel(LoadRAM));
  Multiplexer #(.enable("false")) multiplexer_7 (.in0(CS), .in1(LW), .out(RCS), .sel(LoadRAM));
  Multiplexer #(.enable("false")) multiplexer_8 (.in0(R_W), .in1(LW), .out(R_R_W), .sel(LoadRAM));
  Multiplexer #(.enable("false")) multiplexer_9 (.in0(R_W), .in1(LW), .out(R_R_W), .sel(LoadRAM));
  // Pins of 16 and 32 bits meet at I3

  // Other names for the same wires on the sheet: RI0[31:0] = I1

  // Notes on the sheet:
  //   NO MODIFICAR
  //   Keyboard
endmodule

module RAM (
  input  [15:0] Address,
  input  [31:0] Data_In_0,
  input  [31:0] Data_In_1,
  input  [31:0] Data_In_2,
  input  [31:0] Data_In_3,
  input  [3:0] Mask,
  input  nRead_Write,
  input  Chip_Select,
  input  Reset,
  output [31:0] Data_Out_0,
  output [31:0] Data_Out_1,
  output [31:0] Data_Out_2,
  output [31:0] Data_Out_3,
  output [3:0] out_14,
  output [3:0] Write_Time
);

  wire and_1_out, and_2_out, and_3_out, and_4_out, and_5_out, and_6_out, and_7_out, and_8_out, and_9_out,
       Changed, CLK, comparator_2_eq, comparator_3_eq, comparator_4_eq, comparator_5_eq, comparator_6_eq,
       Count, demultiplexer_3_out0, Idle, Idle_q, Load, Load0, nand_1_out, or_1_out, or_2_out, or_3_out,
       or_4_out, or_5_p1, or_6_out, or_7_out, or_8_out, or_9_out, or_10_out, Proc_q, Proc_qn, undriven_2,
       undriven_3, undriven_4, Update_Mem, Zero_Time;
  wire [3:0] counter_1_q, multiplexer_1_out, subtractor_1_out;
  wire [31:0] Load1, register_1_q, register_2_q, register_3_q, register_4_q, undriven;

  // Probe on 4'b0011
  // Probe on 4'b0010
  Multiplexer #(.width(4), .enable("false")) multiplexer_1 (
    .in0(4'b0011), .in1(4'b0010), .out(multiplexer_1_out), .sel(nRead_Write));
  or or_1 (or_1_out, Idle, Update_Mem);
  or or_2 (or_2_out, ~Chip_Select, Reset);  // OR_Gate
  Subtractor #(.width(4)) subtractor_1 (.a(multiplexer_1_out), .b(4'b0010), .out(subtractor_1_out));  // open: bin, bout
  D_Flip_Flop u_Idle (.clk(CLK), .D(or_1_out), .Q(Idle_q), .preset(or_2_out));  // open: Qn, en, reset
  Demultiplexer #(.enable("false")) demultiplexer_1 (.out0(Idle), .out1(Load0), .in(Idle_q), .sel(Changed));
  // Probe on counter_1_q
  // Probe on counter_1_q
  Counter #(.width(4), .max('hf)) counter_1 (
    .load(Load), .D(subtractor_1_out), .count(Count), .Q(counter_1_q), .clk(CLK), .clr(or_3_out));  // open: carry
  or or_3 (or_3_out, ~Chip_Select, Reset);  // OR_Gate
  Comparator #(.width(4), .mode("unsigned")) comparator_1 (
    .a(4'b0000), .b(counter_1_q), .eq(Zero_Time));  // open: gt, lt
  or or_4 (or_4_out, Count, Load0, Load1[0]);
  Register #(.width(32)) register_1 (.D(Data_In_0), .en(Chip_Select), .Q(register_1_q), .clk(CLK), .clr(or_5_p1));
  // OR_Gate #(.width(4), .value('h3)) or_5: pin names not known; wires that end beside it: or_5_p1, Reset, Chip_Select
  Register #(.width(32)) register_2 (.D(Data_In_1), .en(Chip_Select), .Q(register_2_q), .clk(CLK), .clr(or_6_out));
  or or_6 (or_6_out, ~Chip_Select, Reset);  // OR_Gate
  Register #(.width(32)) register_3 (.D(Data_In_2), .en(Chip_Select), .Q(register_3_q), .clk(CLK), .clr(or_7_out));
  or or_7 (or_7_out, ~Chip_Select, Reset);  // OR_Gate
  Register #(.width(32)) register_4 (.D(Data_In_3), .en(CLK), .Q(register_4_q), .clk(CLK), .clr(or_8_out));
  or or_8 (or_8_out, ~Chip_Select, Reset);  // OR_Gate
  or or_9 (or_9_out, ~Chip_Select, Reset);  // OR_Gate
  D_Flip_Flop Proc (
    .clk(nRead_Write), .D(or_4_out), .Q(Proc_q), .Qn(Proc_qn), .preset(undriven_2), .en(undriven_3),
    .reset(or_10_out));
  D_Flip_Flop Proc_2 (
    .clk(nRead_Write), .D(or_4_out), .Q(Proc_q), .Qn(Proc_qn), .preset(undriven_2), .en(undriven_3),
    .reset(or_10_out));
  or or_10 (or_10_out, ~Address[0], Reset);  // OR_Gate
  Demultiplexer #(.enable("false")) demultiplexer_2 (
    .out0(Count), .out1(Update_Mem), .in(demultiplexer_3_out0), .sel(Zero_Time));
  Demultiplexer #(.enable("false")) demultiplexer_3 (
    .out0(demultiplexer_3_out0), .out1(Load1[0]), .in(Proc_q), .sel(Changed));
  Clock clock_1 (.out(CLK));
  Comparator #(.width(32)) comparator_2 (.a(register_1_q), .b(Data_In_0), .eq(comparator_2_eq));  // open: gt, lt
  Comparator #(.width(32)) comparator_3 (.a(register_2_q), .b(Data_In_1), .eq(comparator_3_eq));  // open: gt, lt
  Comparator #(.width(32)) comparator_4 (.a(register_3_q), .b(Data_In_2), .eq(comparator_4_eq));  // open: gt, lt
  Comparator #(.width(32)) comparator_5 (.a(register_4_q), .b(Data_In_3), .eq(comparator_5_eq));  // open: gt, lt
  Comparator #(.width(32)) comparator_6 (
    .a(undriven), .b({{11{1'b1}}, nRead_Write, Mask[3:2], Mask[3], Mask[0], Address}), .eq(comparator_6_eq));  // open: gt, lt
  nand nand_1 (nand_1_out, comparator_6_eq, comparator_2_eq, comparator_3_eq, comparator_4_eq, comparator_5_eq);
  and and_1 (and_1_out, nand_1_out, Chip_Select);
  or or_11 (Load, Count, Load1[0], Load0);
  and and_2 (and_2_out, Mask[0], Update_Mem, nRead_Write);
  and and_3 (and_3_out, Mask[1], Update_Mem, nRead_Write);
  and and_4 (and_4_out, Mask[2], Update_Mem, nRead_Write);
  and and_5 (and_5_out, Mask[3], Update_Mem, nRead_Write);
  RAM_part #(.addrWidth(16), .dataWidth(32), .bus("separate")) ram_1 (
    .addr(Address), .din(Data_In_0), .data(Data_Out_0), .str(and_2_out), .sel(Chip_Select), .clk(CLK),
    .ld(and_6_out), .clr(Reset));
  and and_6 (and_6_out, ~nRead_Write, Idle);  // AND_Gate
  RAM_part #(.addrWidth(16), .dataWidth(32), .bus("separate")) ram_2 (
    .addr(Address), .din(Data_In_1), .data(Data_Out_0), .str(and_3_out), .sel(Chip_Select), .clk(CLK),
    .ld(and_7_out), .clr(Reset));
  and and_7 (and_7_out, ~nRead_Write, Idle);  // AND_Gate
  RAM_part #(.addrWidth(16), .dataWidth(32), .bus("separate")) ram_3 (
    .addr(Address), .din(Data_In_2), .data(Data_In_3), .str(and_4_out), .sel(undriven_4), .clk(CLK),
    .ld(and_8_out), .clr(Reset));
  and and_8 (and_8_out, ~nRead_Write, Idle);  // AND_Gate
  RAM_part #(.addrWidth(16), .dataWidth(32), .bus("separate")) ram_4 (
    .addr(Address), .din(Load1), .data(Data_Out_3), .str(and_5_out), .sel(Chip_Select), .clk(CLK),
    .ld(and_9_out), .clr(Reset));
  and and_9 (and_9_out, ~nRead_Write, Idle);  // AND_Gate
  // Pins of 1 and 32 bits meet at Load1
  // Pins of 1 and 16 bits meet at Address

  assign Data_Out_1 = Data_Out_0;
  assign Data_Out_2 = Data_In_3;
  assign out_14 = 4'b0011;
  assign Write_Time = 4'b0010;

  // Other names for the same wires on the sheet: M0 = Mask[0]; M2 = Mask[2]; M3 = Mask[3]; RW = nRead_Write;
  //   CLR = Reset; CS = Chip_Select; Load2 = Count; M1 = Mask[1]

  // Notes on the sheet:
  //   NO MODIFICAR
  //   BANK0
  //   BANK1
  //   BANK2
  //   BANK3
endmodule

module S_MIPS (
  input  [31:0] RAM_Out_0,
  input  [31:0] RAM_Out_1,
  input  [31:0] RAM_Out_2,
  input  [31:0] RAM_Out_3,
  input  [3:0] Read_Time,
  input  [3:0] Write_Time,
  input  Kbd_Available,
  input  [6:0] Kbd_ASCII_Data,
  input  Reset,
  input  Clock,
  output [31:0] RAM_In_0,
  output [31:0] RAM_In_1,
  output [31:0] RAM_In_2,
  output [31:0] RAM_In_3,
  output [3:0] Mask,
  output [15:0] Address,
  output TTY_Enable,
  output [6:0] TTY_ASCII_Data,
  output nRead_Write,
  output Chip_Select,
  output Kbd_Enable,
  output Kbd_Clear,
  output [31:0] Stop
);

  wire controlunit_1_p20, controlunit_1_p21, controlunit_1_p22, controlunit_1_p23, controlunit_1_p24,
       controlunit_1_p25, controlunit_1_p26, controlunit_1_p27, datapath_1_p1, RAM_Ready, RI_Start, RI_Write;
  wire [1:0] Bank;
  wire [5:0] FuncCode, OpCode;
  wire [31:0] Address_t, RAM_Data, RAM_OUTPUT_1, RAM_OUTPUT_2, To_RAM;

  // ControlUnit controlunit_1: pin names not known; wires that end beside it: FuncCode, OpCode, RAM_Ready, Kbd_Enable, TTY_Enable, Clock, RI_Write, Reset, Address_t, RAM_Out_0, RAM_OUTPUT_1, RAM_OUTPUT_2, RAM_Out_3, RI_Start, Read_Time, Write_Time, RI_Write, RI_Start, Stop, controlunit_1_p20, controlunit_1_p21, controlunit_1_p22, controlunit_1_p23, controlunit_1_p24, controlunit_1_p25, controlunit_1_p26, controlunit_1_p27, controlunit_1_p22, controlunit_1_p23, controlunit_1_p24, controlunit_1_p25, controlunit_1_p26, controlunit_1_p27
  // MemoryManager memorymanager_1: pin names not known; wires that end beside it: Clock, Reset, Clock, RAM_Data, Mask, Address, Bank, Chip_Select, nRead_Write, RAM_Ready, Reset
  // DataPath datapath_1: pin names not known; wires that end beside it: datapath_1_p1, RAM_Data, Kbd_Available, Kbd_ASCII_Data, OpCode, FuncCode, Address_t, To_RAM, TTY_ASCII_Data
  Demultiplexer #(.select(2), .width(32), .enable("false")) demultiplexer_1 (
    .out0(RAM_In_0), .out1(RAM_In_1), .out2(RAM_In_2), .out3(RAM_In_3), .in(To_RAM), .sel(Bank));
  // Pins of 1 and 32 bits meet at Stop

  assign Kbd_Clear = Reset;

  // Other names for the same wires on the sheet: CLK = Clock; CS = Chip_Select; KBD_AVAIL = Kbd_Available;
  //   KBD_DATA[6:0] = Kbd_ASCII_Data; RAM_A[15:0] = Address; RAM_MASK[3:0] = Mask; RAM_OUTPUT_0[31:0] = RAM_Out_0;
  //   RAM_OUTPUT_3[31:0] = RAM_Out_3; RST = Reset; RW = nRead_Write; TTY_DATA[6:0] = TTY_ASCII_Data;
  //   TTY_EN = TTY_Enable

  // Notes on the sheet:
  //   RAM TIMING
  //   KEYBOARD
  //   SEQUENCING
  //   DATA FROM RAM
  //   RAM ADDRESS
  //   TTY
  //   RAM CONTROL
  //   KEYBOARD
  //   DATA TO RAM
  //   DATA WRITE MASK
endmodule

module RAM_Dispatcher (
  input  [3:0] WriteTime,
  input  Clock,
  input  CLR,
  output [31:0] Data,
  output [15:0] Address,
  output [3:0] Mask,
  output Finished,
  output Write
);

  wire comparator_2_gt, comparator_2_lt, demultiplexer_2_out1, demultiplexer_3_out1, End, IDLE_q, IncAddr,
       Load, or_1_out, or_2_out, While_q, WriteEnd;
  wire [3:0] counter_1_q, undriven;
  wire [31:0] CurrentAddress_q;

  Counter #(.width(32), .max('hffffffff)) CurrentAddress (
    .count(IncAddr), .Q({CurrentAddress_q[31:18], Address, CurrentAddress_q[1:0]}), .clk(Clock), .clr(CLR));  // open: load, D, carry
  or or_1 (or_1_out, IncAddr, demultiplexer_3_out1, Finished);
  D_Flip_Flop IDLE (.clk(Clock), .D(or_1_out), .Q(IDLE_q), .preset(CLR));  // open: Qn, en, reset
  Demultiplexer #(.enable("false")) demultiplexer_1 (.out0(Load), .out1(Finished), .in(IDLE_q), .sel(End));
  D_Flip_Flop While (.clk(Clock), .D(or_2_out), .Q(While_q), .reset(CLR));  // open: Qn, preset, en
  or or_2 (or_2_out, Write, Load);
  RAM_part #(.addrWidth(18), .dataWidth(32)) ram_1 (
    .addr({Address, CurrentAddress_q[1:0]}), .data(Data), .clk(CLR));  // open: sel, ld, clr
  Demultiplexer #(.enable("false")) demultiplexer_2 (
    .out0(Write), .out1(demultiplexer_2_out1), .in(While_q), .sel(WriteEnd));
  Decoder #(.select(2)) decoder_1 (
    .out0(Mask[0]), .out1(Mask[1]), .out2(Mask[2]), .out3(Mask[3]), .sel(CurrentAddress_q[1:0]));  // open: en
  Demultiplexer #(.enable("false")) demultiplexer_3 (
    .out0(IncAddr), .out1(demultiplexer_3_out1), .in(demultiplexer_2_out1), .sel(End));
  Counter #(.width(4), .max('hf)) counter_1 (
    .load(Load), .D(WriteTime), .count(Write), .Q(counter_1_q), .clk(Clock));  // open: carry, clr
  Comparator #(.width(32)) comparator_1 (.a(Data), .b({32{1'b1}}), .eq(End));  // open: gt, lt
  Comparator #(.width(4)) comparator_2 (
    .a(undriven), .b(counter_1_q), .gt(comparator_2_gt), .eq(WriteEnd), .lt(comparator_2_lt));
  Comparator #(.width(4)) comparator_3 (
    .a(undriven), .b(counter_1_q), .gt(comparator_2_gt), .eq(WriteEnd), .lt(comparator_2_lt));

  // Other names for the same wires on the sheet: CLK = Clock; Count = Write; WT[3:0] = WriteTime
endmodule
